// Logisim project control-logic.circ as structural Verilog: 1 circuit, main circuit control_logic
module control_logic (
  input  [31:0] Instruction,
  input  BrEq,
  input  BrLt,
  output PCSel,
  output RegWEn,
  output [2:0] ImmSel,
  output BrUn,
  output ASel,
  output BSel,
  output [3:0] ALUSel,
  output MemWEn,
  output [1:0] WBSel
);

  wire and_10_out, and_11_out, and_12_out, and_13_out, and_14_out, and_15_out, comparator_1_eq,
       comparator_2_eq, comparator_3_eq, comparator_4_eq, comparator_5_eq, comparator_6_eq, comparator_7_eq,
       comparator_8_eq, comparator_9_eq, comparator_10_eq, comparator_11_eq, comparator_12_eq,
       comparator_13_eq, comparator_14_eq, demultiplexer_1_out0, demultiplexer_1_out1, demultiplexer_1_out5,
       demultiplexer_2_out5, is_add, is_addi, is_and, is_andi, is_auipc, is_beq, is_bge, is_bgeu, is_blt,
       is_bltu, is_bne, is_jal, is_jalr, is_lb, is_lh, is_lui, is_lw, is_mul, is_mulh, is_mulhu, is_or,
       is_ori, is_sb, is_sh, is_sll, is_slli, is_slt, is_slti, is_sra, is_srai, is_srl, is_srli, is_sub,
       is_sw, is_xor, is_xori, not_1_out, not_2_out, not_3_out, or_1_out, or_2_out;
  wire [5:0] ROMInput;
  wire [15:14] rom_1_data;
  wire [63:36] undriven;

  Demultiplexer #(.select(3)) demultiplexer_1 (
    .out0(demultiplexer_1_out0), .out1(demultiplexer_1_out1), .out2(is_slt), .out3(is_mulhu), .out4(is_xor),
    .out5(demultiplexer_1_out5), .out6(is_or), .out7(is_and), .in(comparator_1_eq), .sel(Instruction[14:12]));
  Comparator #(.mode("unsigned"), .width(7)) comparator_1 (
    .a(Instruction[6:0]), .b(7'b0110011), .eq(comparator_1_eq));  // open: gt, lt
  Demultiplexer #(.select(3)) demultiplexer_2 (
    .out0(is_addi), .out1(is_slli), .out2(is_slti), .out4(is_xori), .out5(demultiplexer_2_out5),
    .out6(is_ori), .out7(is_andi), .in(comparator_2_eq), .sel(Instruction[14:12]));  // open: out3
  Comparator #(.mode("unsigned"), .width(7)) comparator_2 (
    .a(Instruction[6:0]), .b(7'b0010011), .eq(comparator_2_eq));  // open: gt, lt
  Demultiplexer #(.select(3)) demultiplexer_3 (
    .out0(is_beq), .out1(is_bne), .out4(is_blt), .out5(is_bge), .out6(is_bltu), .out7(is_bgeu),
    .in(comparator_3_eq), .sel(Instruction[14:12]));  // open: out2, out3
  Comparator #(.mode("unsigned"), .width(7)) comparator_3 (
    .a(Instruction[6:0]), .b(7'b1100011), .eq(comparator_3_eq));  // open: gt, lt
  ROM #(.addrWidth(6), .dataWidth(16)) rom_1 (
    .addr(ROMInput), .data({rom_1_data, WBSel, MemWEn, ALUSel, BSel, ASel, BrUn, ImmSel, RegWEn}));
  Comparator #(.width(7)) comparator_4 (.a(Instruction[31:25]), .b({7{1'b0}}), .eq(comparator_4_eq));  // open: gt, lt
  Comparator #(.width(7)) comparator_5 (.a(Instruction[31:25]), .b(7'b0000001), .eq(comparator_5_eq));  // open: gt, lt
  Comparator #(.width(7)) comparator_6 (.a(Instruction[31:25]), .b(7'b0100000), .eq(comparator_6_eq));  // open: gt, lt
  Comparator #(.width(7)) comparator_7 (.a(Instruction[31:25]), .b({7{1'b0}}), .eq(comparator_7_eq));  // open: gt, lt
  Comparator #(.width(7)) comparator_8 (.a(Instruction[31:25]), .b(7'b0000001), .eq(comparator_8_eq));  // open: gt, lt
  Comparator #(.width(7)) comparator_9 (.a(Instruction[31:25]), .b({7{1'b0}}), .eq(comparator_9_eq));  // open: gt, lt
  Comparator #(.width(7)) comparator_10 (
    .a(Instruction[31:25]), .b(7'b0100000), .eq(comparator_10_eq));  // open: gt, lt
  and and_1 (is_add, demultiplexer_1_out0, comparator_4_eq);
  and and_2 (is_mul, demultiplexer_1_out0, comparator_5_eq);
  and and_3 (is_sub, demultiplexer_1_out0, comparator_6_eq);
  and and_4 (is_sll, demultiplexer_1_out1, comparator_7_eq);
  and and_5 (is_mulh, demultiplexer_1_out1, comparator_8_eq);
  and and_6 (is_srl, demultiplexer_1_out5, comparator_9_eq);
  and and_7 (is_sra, demultiplexer_1_out5, comparator_10_eq);
  and and_8 (is_srli, demultiplexer_2_out5, comparator_11_eq);
  Comparator #(.width(7)) comparator_11 (.a(Instruction[31:25]), .b({7{1'b0}}), .eq(comparator_11_eq));  // open: gt, lt
  and and_9 (is_srai, demultiplexer_2_out5, comparator_12_eq);
  Comparator #(.width(7)) comparator_12 (
    .a(Instruction[31:25]), .b(7'b0100000), .eq(comparator_12_eq));  // open: gt, lt
  Demultiplexer #(.select(3)) demultiplexer_4 (
    .out0(is_lb), .out1(is_lh), .out2(is_lw), .in(comparator_13_eq), .sel(Instruction[14:12]));  // open: out3, out4, out5, out6, out7
  Comparator #(.mode("unsigned"), .width(7)) comparator_13 (
    .a(Instruction[6:0]), .b(7'b0000011), .eq(comparator_13_eq));  // open: gt, lt
  Demultiplexer #(.select(3)) demultiplexer_5 (
    .out0(is_sb), .out1(is_sh), .out2(is_sw), .in(comparator_14_eq), .sel(Instruction[14:12]));  // open: out3, out4, out5, out6, out7
  Comparator #(.mode("unsigned"), .width(7)) comparator_14 (
    .a(Instruction[6:0]), .b(7'b0100011), .eq(comparator_14_eq));  // open: gt, lt
  Comparator #(.mode("unsigned"), .width(7)) comparator_15 (
    .a(Instruction[6:0]), .b(7'b0010111), .eq(is_auipc));  // open: gt, lt
  Comparator #(.mode("unsigned"), .width(7)) comparator_16 (
    .a(Instruction[6:0]), .b(7'b0110111), .eq(is_lui));  // open: gt, lt
  Comparator #(.mode("unsigned"), .width(7)) comparator_17 (
    .a(Instruction[6:0]), .b(7'b1101111), .eq(is_jal));  // open: gt, lt
  Comparator #(.mode("unsigned"), .width(7)) comparator_18 (
    .a(Instruction[6:0]), .b(7'b1100111), .eq(is_jalr));  // open: gt, lt
  and and_10 (and_10_out, BrEq, is_beq);
  not not_1 (not_1_out, BrEq);
  and and_11 (and_11_out, not_1_out, is_bne);
  and and_12 (and_12_out, BrLt, is_blt);
  and and_13 (and_13_out, BrLt, is_bltu);
  not not_2 (not_2_out, BrLt);
  and and_14 (and_14_out, not_2_out, is_bge);
  not not_3 (not_3_out, BrLt);
  and and_15 (and_15_out, not_3_out, is_bgeu);
  or or_1 (or_1_out, and_10_out, and_11_out, and_12_out, and_13_out, and_14_out, and_15_out);
  or or_2 (or_2_out, is_jal, is_jalr);
  or or_3 (PCSel, or_1_out, or_2_out);
  Priority_Encoder #(.select_enc(6)) priority_encoder_1 (
    .in0(is_add), .in1(is_mul), .in2(is_sub), .in3(is_sll), .in4(is_mulh), .in5(is_mulhu), .in6(is_slt),
    .in7(is_xor), .in8(is_srl), .in9(is_sra), .in10(is_or), .in11(is_and), .in12(is_lb), .in13(is_lh),
    .in14(is_lw), .in15(is_addi), .in16(is_slli), .in17(is_slti), .in18(is_xori), .in19(is_srli),
    .in20(is_srai), .in21(is_ori), .in22(is_andi), .in23(is_sb), .in24(is_sh), .in25(is_sw), .in26(is_beq),
    .in27(is_bne), .in28(is_blt), .in29(is_bge), .in30(is_bltu), .in31(is_bgeu), .in32(is_auipc),
    .in33(is_lui), .in34(is_jal), .in35(is_jalr), .in36(undriven[36]), .in37(undriven[37]),
    .in38(undriven[38]), .in39(undriven[39]), .in40(undriven[40]), .in41(undriven[41]), .in42(undriven[42]),
    .in43(undriven[43]), .in44(undriven[44]), .in45(undriven[45]), .in46(undriven[46]), .in47(undriven[47]),
    .in48(undriven[48]), .in49(undriven[49]), .in50(undriven[50]), .in51(undriven[51]), .in52(undriven[52]),
    .in53(undriven[53]), .in54(undriven[54]), .in55(undriven[55]), .in56(undriven[56]), .in57(undriven[57]),
    .in58(undriven[58]), .in59(undriven[59]), .in60(undriven[60]), .in61(undriven[61]), .in62(undriven[62]),
    .in63(undriven[63]), .out(ROMInput));  // open: gs, en_out, en_in

  // Other names for the same wires on the sheet: opcode[6:0] = Instruction[6:0]; funct3[2:0] = Instruction[14:12];
  //   funct7[6:0] = Instruction[31:25]

  // Notes on the sheet:
  //   INPUTS to your circuit
  //   0b0110011
  //   "R" Instructions
  //   0b0010011
  //   "I" Instructions
  //   0b1100011
  //   "B" Instructions
  //   contents of rom_1 (hex, n*v repeats v):
  //   1001 1401 1601 1081 1481 1581 1101 1201 1281 1681 1301 1381 41 41 41 1041 10c1 1141 1241 12c1 16c1
  //   1341 13c1 842 842 842 4*64 74 74 1067 17c7 2069 2041
  //   ROM FOR CONTROL LOGIC
  //   DON'T CHANGE THE LOCATIONS OF THE INPUTS AND OUTPUTS!
  //   This is only if you choose to do the ROM option
  //   OUTPUT from your circuit
  //   0b0000011
  //   Load Instructions
  //   0b0100011
  //   Save Instructions
  //   0b0010111
  //   auipc
  //   0b0110111
  //   lui
  //   0b1101111
  //   jal
  //   0b1100111
  //   jalr
  //   PCSel Logic
  //   (If any of these break conditions are satisfied, PC += offset)
  //   (if jal or jalr, PCSel = 1)
endmodule
