// Logisim project cpu.circ as structural Verilog: 1 circuit, main circuit cpu
module cpu (
  input  clk,
  input  [31:0] Instruction,
  input  [31:0] MemReadData,
  output [31:0] MemAddress,
  output [31:0] ProgramCounter,
  output [31:0] ra,
  output [31:0] sp,
  output [31:0] t0,
  output [31:0] t1,
  output [31:0] t2,
  output [31:0] s0,
  output [31:0] s1,
  output [31:0] a0,
  output [3:0] MemWriteMask,
  output [31:0] MemWriteData
);

  wire ASel, BrEq, BrLt, BrUn, BSel, MemWEn, PCSel, RegWEn;
  wire [1:0] WBSel;
  wire [2:0] ImmSel;
  wire [3:0] ALUSel;
  wire [31:0] Imm_genResult, Instruction_EX, Instruction_IF, multiplexer_1_out, multiplexer_3_out,
       multiplexer_4_out, partial_load_1_datatoreg, pc_add4_EX, pc_add4_IF, ProgramCounter_EX, ReadData1,
       ReadData2, wb;

  Adder #(.width(32)) adder_1 (.a(ProgramCounter), .b(32'h4), .out(pc_add4_IF));  // open: cin, cout
  Register #(.width(32)) PC (.D(multiplexer_1_out), .clk(clk), .Q(ProgramCounter));  // open: en, clr
  Multiplexer #(.width(32)) multiplexer_1 (.in0(pc_add4_IF), .in1(MemAddress), .out(multiplexer_1_out), .sel(PCSel));
  Multiplexer #(.width(32)) multiplexer_2 (.in0(Instruction), .in1(32'h13), .out(Instruction_IF), .sel(PCSel));
  Register #(.width(32)) register_1 (.D(ProgramCounter), .clk(clk), .Q(ProgramCounter_EX));  // open: en, clr
  Register #(.width(32)) register_2 (.D(pc_add4_IF), .clk(clk), .Q(pc_add4_EX));  // open: en, clr
  Register #(.width(32)) register_3 (.D(Instruction_IF), .clk(clk), .Q(Instruction_EX));  // open: en, clr
  regfile regfile_1 (
    .ReadIndex1(Instruction_EX[19:15]), .ReadIndex2(Instruction_EX[24:20]),
    .WriteIndex(Instruction_EX[11:7]), .WriteData(wb), .RegWEn(RegWEn), .clk(clk), .ra(ra), .sp(sp), .t0(t0),
    .t1(t1), .t2(t2), .s0(s0), .s1(s1), .a0(a0), .ReadData1(ReadData1), .ReadData2(ReadData2));
  imm_gen imm_gen_1 (.Instruction(Instruction_EX), .ImmSel(ImmSel), .Immediate(Imm_genResult));
  control_logic control_logic_1 (
    .PCSel(PCSel), .RegWEn(RegWEn), .ImmSel(ImmSel), .BrUn(BrUn), .ASel(ASel), .BSel(BSel), .ALUSel(ALUSel),
    .MemWEn(MemWEn), .WBSel(WBSel), .Instruction(Instruction_EX), .BrEq(BrEq), .BrLt(BrLt));
  Multiplexer #(.width(32)) multiplexer_3 (
    .in0(ReadData1), .in1(ProgramCounter_EX), .out(multiplexer_3_out), .sel(ASel));
  Multiplexer #(.width(32)) multiplexer_4 (.in0(ReadData2), .in1(Imm_genResult), .out(multiplexer_4_out), .sel(BSel));
  branch_comp branch_comp_1 (.BrData1(ReadData1), .BrData2(ReadData2), .BrUn(BrUn), .BrEq(BrEq), .BrLt(BrLt));
  alu alu_1 (.ALUResult(MemAddress), .A(multiplexer_3_out), .B(multiplexer_4_out), .ALUSel(ALUSel));
  partial_store partial_store_1 (
    .Instruction(Instruction_EX), .MemAddress(MemAddress), .DataFromReg(ReadData2), .MemWEn(MemWEn),
    .MemWriteMask(MemWriteMask), .DataToMem(MemWriteData));
  partial_load partial_load_1 (
    .Instruction(Instruction_EX), .MemAddress(MemAddress), .DataFromMem(MemReadData),
    .DataToReg(partial_load_1_datatoreg));
  Multiplexer #(.select(2), .width(32)) multiplexer_5 (
    .in0(partial_load_1_datatoreg), .in1(MemAddress), .in2(pc_add4_EX), .out(wb), .sel(WBSel));  // open: in3

  // Other names for the same wires on the sheet: ALUResult[31:0] = MemAddress; rd[4:0] = Instruction_EX[11:7];
  //   rs1[4:0] = Instruction_EX[19:15]; rs2[4:0] = Instruction_EX[24:20]; ProgramCounter_IF[31:0] = ProgramCounter

  // Notes on the sheet:
  //   To IMEM
  //   IMEM (do **NOT** move this)
  //   From IMEM
  //   Inputs/Outputs for testing. Do **NOT** move these.
  //   It is OK to move the PC, RegFile, ALU, MEM, Branch Comp, Imm Gen, Partial Load, Partial Store and Control Logic to wherever is most convenient for you when constructing your CPU, and to delete this text
  //   To DMEM
  //   DMEM (do **NOT** move this)
  //   From DMEM
endmodule
