// Logisim project partial-store.circ as structural Verilog: 1 circuit, main circuit partial_store
module partial_store (
  input  [31:0] Instruction,
  input  [31:0] MemAddress,
  input  [31:0] DataFromReg,
  input  MemWEn,
  output [3:0] MemWriteMask,
  output [31:0] DataToMem
);

  wire comparator_1_eq;
  wire [2:0] multiplexer_4_out, PartialStoreSel;

  Comparator #(.width(3)) comparator_1 (.a(Instruction[14:12]), .b(3'b010), .eq(comparator_1_eq));  // open: gt, lt
  Multiplexer #(.width(3)) multiplexer_1 (
    .in0({Instruction[12], MemAddress[1:0]}), .in1(3'b111), .out(PartialStoreSel), .sel(comparator_1_eq));
  Multiplexer #(.select(3), .width(32)) multiplexer_2 (
    .in0({{24{1'b0}}, DataFromReg[7:0]}), .in1({{16{1'b0}}, DataFromReg[7:0], {8{1'b0}}}),
    .in2({{8{1'b0}}, DataFromReg[7:0], {16{1'b0}}}), .in3({DataFromReg[7:0], {24{1'b0}}}),
    .in4({{16{1'b0}}, DataFromReg[15:0]}), .in6({DataFromReg[15:0], {16{1'b0}}}), .in7(DataFromReg),
    .out(DataToMem), .sel(PartialStoreSel));  // open: in5
  Multiplexer #(.select(3), .width(4)) multiplexer_3 (
    .in0(4'b0001), .in1(4'b0010), .in2(4'b0100), .in3(4'b1000), .in4(4'b0011), .in5(4'b0000), .in6(4'b1100),
    .in7(4'b1111), .out(MemWriteMask), .sel(multiplexer_4_out));
  Multiplexer #(.width(3)) multiplexer_4 (.in0(3'b101), .in1(PartialStoreSel), .out(multiplexer_4_out), .sel(MemWEn));

  // Other names for the same wires on the sheet: lsb_2_addr[1:0] = MemAddress[1:0]; funct3[2:0] = Instruction[14:12];
  //   opcode[6:0] = Instruction[6:0]; funct7[6:0] = Instruction[31:25]

  // Notes on the sheet:
  //   INPUTS to your circuit
  //   DON'T CHANGE THE LOCATIONS OF THE INPUTS AND OUTPUTS!
  //   OUTPUT from your circuit
endmodule
